# Fritzing sketch LEDTimedCandle (saved by Fritzing 0.9.1b)
breadboards: 1

parts:
  U2 = ATTINY13 [package=dip]
  R1 = Resistor [tolerance=±5% resistance=10k package=THT]
  R2 = Resistor [tolerance=±5% resistance=220 package=THT]
  LED1 = LED - 5mm [color="Yellow (592nm)" package="5 mm [THT]"]
  LED2 = LED - 5mm [color="Red (633nm)" package="5 mm [THT]"]
  R3 = Resistor [tolerance=±5% resistance=220 package=THT]
  V1 = DC Power [voltage=3V]
  C1 = Ceramic Capacitor [capacitance=100nF package="100 mil [THT, multilayer]"]

nets:
  N1: U2.PB5(NRES), R1.Pin_1
  N2: U2.PB3(ADC3), R2.Pin_0
  N3: U2.PB4(ADC2), R3.Pin_0
  GND: U2.GND, LED1.cathode, LED2.cathode, V1.V-, C1.0
  N4: U2.VCC, R1.Pin_0, V1.V+, C1.1
  N5: R2.Pin_1, LED1.anode
  N6: LED2.anode, R3.Pin_1
